# Fritzing sketch Car_Control (saved by Fritzing 0.9.9b)
breadboards: 1

parts:
  ESP32_-_Back1 = ESP32 - CAM
  L298N1 = L298N DC motor driver
  DHT11_1 = DHT11 module
  HC-SR04_Sensor_1 = HC-SR04 Ultrasonic Distance Sensor
  M1 = gear-motor
  M2 = gear-motor
  M3 = gear-motor
  M4 = gear-motor
  VCC1 = 4 x AAA Battery Mount
  J1 = Basic Servo
  U2 = LuaNode32 / ESP32 [part_number=ESP32S-PIN30]

nets:
  N1: ESP32_-_Back1.GPIO13, U2.D4
  N2: ESP32_-_Back1.GPIO12, U2.D2
  GND: ESP32_-_Back1.GND, L298N1.GND, DHT11_1.GND, HC-SR04_Sensor_1.GND, VCC1.-, J1.gnd, U2.GND
  5V: ESP32_-_Back1.5V, L298N1.5V, HC-SR04_Sensor_1.VCC, J1.vcc, U2.Vin
  N3: L298N1.OUT1, M2.pin_1, M4.pin_1
  N4: L298N1.OUT2, M2.pin_2, M4.pin_2
  N5: L298N1.OUT3, M1.pin_1, M3.pin_1
  N6: L298N1.OUT4, M1.pin_2, M3.pin_2
  N7: L298N1.12V, VCC1.+
  N8: L298N1.IN1, U2.D13
  N9: L298N1.IN2, U2.D12
  N10: L298N1.IN3, U2.D14
  N11: L298N1.IN4, U2.D27
  VCC: DHT11_1.VCC, U2.3V3
  N12: DHT11_1.DATA, U2.D15
  N13: HC-SR04_Sensor_1.TRIG, U2.D25
  N14: HC-SR04_Sensor_1.ECHO, U2.D33
  N15: J1.pulse, U2.D26

custom parts:
  ESP32 - CAM: The ESP32-CAM has a very competitive small-size camera module that can operate independently as a minimum system with a footprint of only 27*40.5*4.5mm and a deep sleep current of up to 6mA.
  L298N DC motor driver: 2x DC motor driver with 78M05 positive voltage regulator (7..35 V) L298N: max 46 V, 2 A Set 5 V Enable jumper to enable 5 V regultor (needed for the L298N) and +5 V output at screw terminal or supply external +5 V at screw terminal Set ENA and/or ENB to +5 V to enable motor permanently or supply ENA and/or ENB with PWM signal IN1 and IN2 set rotation directory for motor A (OUT1/OUT2) IN2 and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
  DHT11 module: https://cdn-learn.adafruit.com/downloads/pdf/dht.pdf DHT11 black pcb module reference by:https://github.com/adafruit/Fritzing-Library/blob/master/parts/DHT11%20Humitidy%20and%20Temperature%20Sensor.fzpz
  LuaNode32 / ESP32: New Image for LuaNode32 DOIT ESP32 DEVKIT V1. Base parts from LuaNode32 / ESP32 ESP32 based LuaNode32 by G.Noorlander DOIT Esp32 DevKit v1 (30 pins long, 11 pins width) by Werner Rothschopf (modified by vanepp Dec 2018)
